# Fritzing sketch board_layout (saved by Fritzing 0.9.8b)
perfboards: 1

parts:
  J6 = male pin header, 3 pins [form="♂ (male)"]  # not connected
  J7 = female pin header, 10 pins [form="♀ (female)"]
  J8 = female pin header, 15 pins [form="♀ (female)"]  # not connected
  J9 = female pin header, 15 pins [form="♀ (female)"]
  U6 = ESP 32 DEVKIT DOIT  # not connected
  J10 = Power Jack [package=power_jack_smd]  # not connected
  Part3 = Adafruit ADS1115 16Bit I2C ADC [part_number="Adafruit #1085"]  # not connected
  S2 = PH meter [package=THT]  # not connected

nets:
  N1: J7.pin6, J7.pin9, J9.pin2
  N2: J7.pin7, J9.pin12
  N3: J7.pin8, J9.pin14

notes:
  ADS115
  PH Meter
  DC Power
  ESP 32

custom parts:
  Adafruit ADS1115 16Bit I2C ADC: For microcontrollers without an analog-to-digital converter or when you want a higher-precision ADC, the ADS1115 provides 16-bit precision at 860 samples/second over I2C. The chip can be configured as 4 single-ended input channels, or two differential channels. As a nice bonus, it even includes a programmable gain amplifier, up to x16, to help boost up smaller single/differential signals to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
